# Fritzing sketch Mood-lamp (saved by Fritzing 0.9.4)
circuit board: 7.13872cm x 6.73804cm
breadboards: 1

parts:
  WeMos_D1_Mini1 = WeMos D1 Mini
  BMP280_Breakout1 = BMP280 Breakout Board [part_number=BMP280]
  part = 24 NeoPixel Ring [part_number=1586]

nets:
  5V: WeMos_D1_Mini1.5V, BMP280_Breakout1.VCC, part.VDD
  N1: WeMos_D1_Mini1.D1, BMP280_Breakout1.SCL
  N2: WeMos_D1_Mini1.D2, BMP280_Breakout1.SDA
  N3: WeMos_D1_Mini1.D3, part.IN
  GND: WeMos_D1_Mini1.G, BMP280_Breakout1.GND, part.GND

notes:
  Lo alimentmos por USB 5V
  ¿Consumo de neopixels?

custom parts:
  BMP280 Breakout Board: This is a breakout board for the Bosch Sensortec BMP280, "an absolute barometric pressure sensor especially designed for mobile applications." The operation range is 300 to 1100 hPa. Supply voltage is 1.2 to 3.6V. Operating temperature range is -40 to +85 °C.
  24 NeoPixel Ring: 24 ultra bright smart LED NeoPixels are arranged in a circle with 2.6" (66mm) outer diameter. The rings are 'chainable' - connect the output pin of one to the input pin of another. Use only one microcontroller pin to control as many as you can chain together! Each LED is addressable as the driver chip is inside the LED. Each one has ~18mA constant current drive so the color will be very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
